// Logisim project project.circ as structural Verilog: 1 circuit, main circuit main
module main (
  input  INPUT,
  input  PRESET,
  input  CLEAR,
  output GREEN,
  output YELLOW,
  output RED
);

  wire A0_q, A1_q, A2_q, A3_q, A3_qn, ClockPulse_out, d_ff_1_q, not_1_out;

  Clock ClockPulse (.out(ClockPulse_out));
  T_Flip_Flop #(.trigger("falling")) A0 (
    .clk(ClockPulse_out), .T(INPUT), .Q(A0_q), .preset(PRESET), .reset(CLEAR));  // open: Qn, en
  T_Flip_Flop #(.trigger("falling")) A1 (
    .clk(A0_q), .T(INPUT), .Q(A1_q), .preset(PRESET), .reset(CLEAR));  // open: Qn, en
  T_Flip_Flop #(.trigger("falling")) A2 (
    .clk(A1_q), .T(INPUT), .Q(A2_q), .preset(PRESET), .reset(CLEAR));  // open: Qn, en
  T_Flip_Flop #(.trigger("falling")) A3 (
    .clk(A2_q), .T(INPUT), .Q(A3_q), .Qn(A3_qn), .preset(PRESET), .reset(CLEAR));  // open: en
  D_Flip_Flop #(.trigger("falling")) d_ff_1 (
    .clk(ClockPulse_out), .D(A3_q), .Q(d_ff_1_q), .reset(CLEAR));  // open: Qn, preset, en
  and and_1 (GREEN, A3_q, not_1_out);
  not not_1 (not_1_out, YELLOW);
  xor xor_1 (YELLOW, A3_q, d_ff_1_q);
  and and_2 (RED, not_1_out, A3_qn);
endmodule
